// Logisim project Single_Cycle_CPU.circ as structural Verilog: 1 circuit, main circuit main
module main (
);

  wire ALUSrc, and_1_out, and_2_out, BneOrBeq, Branch, Clk, clock_1_out, Equal, ExRegWrite, Halt, HasExp,
       IsCOP0, isJAL, isJR, IsRet, IsShamt, Jump, MemtoReg, multiplexer_4_out, not_2_out, not_3_out,
       not_4_out, not_5_out, or_1_out, undriven_2, xor_1_out;
  wire [3:0] undriven_6, undriven_7, undriven_8, undriven_9;
  wire [15:0] undriven_5;
  wire [31:0] adder_1_out, adder_2_out, multiplexer_1_out, multiplexer_3_out, multiplexer_6_out,
       multiplexer_7_out, multiplexer_8_out, multiplexer_9_out, multiplexer_10_out, multiplexer_11_out,
       multiplexer_12_out, ram_1_dout, regfile_1_r1, register_2_q, shifter_1_out, undriven, undriven_3,
       undriven_4;

  Multiplexer #(.width(32)) multiplexer_1 (.in1(undriven), .out(multiplexer_1_out), .sel(and_1_out));  // open: in0
  and and_1 (and_1_out, IsRet, IsCOP0);
  Multiplexer multiplexer_2 (.in0(clock_1_out), .in1(1'b0), .out(Clk), .sel(Halt));
  Clock clock_1 (.out(clock_1_out));
  Multiplexer #(.width(32)) multiplexer_3 (
    .in0({32{1'b0}}), .in1(multiplexer_1_out), .out(multiplexer_3_out), .sel(HasExp));
  not not_1 (HasExp, undriven_2);
  or or_1 (or_1_out, undriven_2, and_1_out);
  Register #(.width(32)) register_1 (.D(multiplexer_3_out), .clk(multiplexer_4_out));  // open: en, Q, clr
  Multiplexer multiplexer_4 (.in0(Clk), .in1(not_2_out), .out(multiplexer_4_out), .sel(or_1_out));
  not not_2 (not_2_out, Clk);
  // control_unit control_unit_1: pin names not known
  Adder #(.width(32)) adder_1 (.b({32{1'b0}}), .out(adder_1_out));  // open: a, cin, cout
  Register #(.width(32)) register_2 (.Q(register_2_q), .clk(HasExp));  // open: D, en, clr
  // CP0 cp0_1: pin names not known; wires that end beside it: Clk, HasExp, ExRegWrite
  Multiplexer #(.width(32)) multiplexer_5 (.in0(undriven_3), .in1(multiplexer_6_out), .sel(not_3_out));  // open: out
  regfile regfile_1 (.R1(regfile_1_r1));  // open: R1A, R2A, RW, Din, we, clk, a0, v0, R2
  not not_3 (not_3_out, IsCOP0);
  not not_4 (not_4_out, isJAL);
  Multiplexer #(.width(32)) multiplexer_6 (
    .in0(adder_1_out), .in1(multiplexer_11_out), .out(multiplexer_6_out), .sel(not_4_out));
  Multiplexer #(.width(32)) multiplexer_7 (.out(multiplexer_7_out), .sel(ALUSrc));  // open: in0, in1
  Multiplexer #(.width(32)) multiplexer_8 (.in0(regfile_1_r1), .out(multiplexer_8_out), .sel(IsShamt));  // open: in1
  Multiplexer #(.width(32)) multiplexer_9 (
    .in0(multiplexer_7_out), .out(multiplexer_9_out), .sel(IsShamt));  // open: in1
  syscall_decoder syscall_decoder_1 (.Halt(Halt));  // open: clk, Enable, v0, a0, Hex
  // alu alu_1: pin names not known; wires that end beside it: multiplexer_9_out
  RAM #(.dataWidth(32)) ram_1 (.addr(undriven_4[7:0]), .dout(ram_1_dout));  // open: we, oe, clk, din
  Shifter #(.width(32)) shifter_1 (.\dist ({5{1'b0}}), .out(shifter_1_out));  // open: in
  xor xor_1 (xor_1_out, Equal, BneOrBeq);
  Hex_Digit_Display hex_digit_display_1 (.value(undriven_9));  // open: dp
  Hex_Digit_Display hex_digit_display_2 (.value(undriven_8));  // open: dp
  Adder #(.width(32)) adder_2 (.b(shifter_1_out), .out(adder_2_out));  // open: a, cin, cout
  Hex_Digit_Display hex_digit_display_3 (.value(undriven_7));  // open: dp
  Hex_Digit_Display hex_digit_display_4 (.value(undriven_6));  // open: dp
  and and_2 (and_2_out, Branch, xor_1_out);
  Hex_Digit_Display hex_digit_display_5 (.value(undriven_5[15:12]));  // open: dp
  Hex_Digit_Display hex_digit_display_6 (.value(undriven_5[11:8]));  // open: dp
  Multiplexer #(.width(32)) multiplexer_10 (.in1(adder_2_out), .out(multiplexer_10_out), .sel(and_2_out));  // open: in0
  Hex_Digit_Display hex_digit_display_7 (.value(undriven_5[7:4]));  // open: dp
  Hex_Digit_Display hex_digit_display_8 (.value(undriven_5[3:0]));  // open: dp
  Multiplexer #(.width(32)) multiplexer_11 (
    .in0(undriven_4), .in1(ram_1_dout), .out(multiplexer_11_out), .sel(MemtoReg));
  Multiplexer #(.width(32)) multiplexer_12 (
    .in1(multiplexer_10_out), .out(multiplexer_12_out), .sel(not_5_out));  // open: in0
  not not_5 (not_5_out, Jump);
  Multiplexer #(.width(32)) multiplexer_13 (.in0(multiplexer_12_out), .in1(regfile_1_r1), .sel(isJR));  // open: out
  // Pins of 8 and 32 bits meet at undriven_4

  // Notes on the sheet:
  //   PC Buffer
endmodule
